# Fritzing sketch wiring_tagtune (saved by Fritzing 0.9.6b)
perfboards: 1

parts:
  A1 = Waveshare rp2040-zero tht [package=THT]
  M1 = PAM8403 Stereo Amplifier [part_number=HW-104]
  U1 = RFID RC522 SIP - 8 pins [chip_label="RFID RC522" package="SIP (Single Inline) [THT]"]
  DFPlayer_Mini1 = DFPlayer MINI [package="DIP (Dual Inline) [THT]"]
  J3 = JST XH_2.54mm Horizontal SMD_Connector 2pin [package=SMD]
  J4 = JST XH_2.54mm Horizontal SMD_Connector 2pin [package=SMD]
  SP1 = SPEAKER [package=pcb_mount_speaker]
  J5 = JST XH_2.54mm Horizontal SMD Connector 3pin [package=SMD]
  J6 = JST XH_2.54mm Horizontal SMD_Connector 2pin [package=SMD]
  J7 = JST XH_2.54mm Horizontal SMD Connector 3pin [package=SMD]
  J8 = JST XH_2.54mm Horizontal SMD Connector 3pin [package=SMD]
  SP2 = SPEAKER [package=pcb_mount_speaker]
  X1 = USB Connectors [package=usb-a-s-nosilk-female]
  Part1 = ws2812b [package="smd 2812b"]
  S2 = Round Pushbutton
  S3 = Round Pushbutton

nets:
  N1: A1.Pin_1, M1.POWER+, J7.pin1, Part1.VDD
  N2: A1.Pin_2, DFPlayer_Mini1.GND#6
  N3: A1.Pin_3, DFPlayer_Mini1.VCC
  N4: A1.Pin_6, J7.pin3, Part1.DIN
  N5: A1.Pin_10, U1.NSS, J5.pin1
  N6: A1.Pin_11, U1.MISO, J5.pin2
  N7: A1.Pin_12, U1.MOSI, J5.pin3
  N8: A1.Pin_13, U1.SCK, J6.pin1
  N9: A1.Pin_14, U1.RST, J6.pin2
  N10: A1.Pin_16, J8.pin1, S2.leg1
  N11: A1.Pin_17, J8.pin2, S3.leg0
  N12: A1.Pin_18, DFPlayer_Mini1.TX
  N13: A1.Pin_19, DFPlayer_Mini1.RX
  N14: A1.Pin_20, DFPlayer_Mini1.BUSY
  N15: M1.ROUT-, SP2.+
  N16: M1.ROUT+, SP2.-
  N17: M1.LOUT+, SP1.-
  N18: M1.LOUT-, SP1.+
  N19: M1.POWER-, DFPlayer_Mini1.GND#9
  N20: M1.INPUTL, DFPlayer_Mini1.SPK2
  N21: M1.INPUTR, DFPlayer_Mini1.SPK1
  N22: U1.GND, J4.pin1
  N23: U1.VCC, J4.pin2
  N24: J3.pin1, X1.GND
  N25: J3.pin2, X1.VBUS
  N26: J7.pin2, Part1.VSS
  N27: S2.leg0, S3.leg1

custom parts:
  Waveshare rp2040-zero tht: .RP2040-Zero, A Low-Cost, High-Performance Pico-Like MCU Board Based On Raspberry Pi Microcontroller RP2040. This varant is THT without the extra connections.
  PAM8403 Stereo Amplifier: PAM8403 stereo amplifier module Descriptive words Links: PAM8403 product datasheet
  RFID RC522 SIP - 8 pins: A SIP stand-in part for RFID RC522 . With 8 pins on a 300 mil single inline package (SIP) footprint.
  DFPlayer MINI: MP3 module by DFRobot.com for playing Music from an SD-Card. Supports WAV and MP3 files.
  JST XH_2.54mm Horizontal SMD_Connector 2pin: JST XH_2.54mm Horizontal SMD_Connector 2pin.
  JST XH_2.54mm Horizontal SMD Connector 3pin: JST XH_2.54mm Horizontal SMD Connector 3pin.
